# Fritzing sketch Bomberman_sketch (saved by Fritzing 0.9.2b)
breadboards: 1

parts:
  Arduino_Uno = Arduino Uno (Rev3)
  LED-Green = LED - 5mm [color="Green (570nm)" package="5 mm [THT]"]
  S1 = Pushbutton [package="[THT]"]
  LED-Red = LED - 5mm [color="Red (633nm)" package="5 mm [THT]"]
  LED-White = LED - 5mm [color="White (4500K)" package="5 mm [THT]"]
  LED-Yellow = LED - 5mm [color="Yellow (595nm)" package="5 mm [THT]"]
  R1-Red = Resistor [tolerance=±5% resistance=220 package=THT]
  R2-White = Resistor [tolerance=±5% resistance=220 package=THT]
  R3-Green = Resistor [tolerance=±5% resistance=220 package=THT]
  R4-Yellow = Resistor [tolerance=±5% resistance=220 package=THT]
  R5-Taster = Resistor [tolerance=±5% resistance=1M package=THT]

nets:
  N1: Arduino_Uno.D9_PWM, R4-Yellow.Pin_0
  N2: Arduino_Uno.D10_PWM/SS, R3-Green.Pin_0
  N3: Arduino_Uno.D11_PWM/MOSI, R2-White.Pin_0
  N4: Arduino_Uno.D12/MISO, R1-Red.Pin_0
  N5: Arduino_Uno.GND, R5-Taster.Pin_0
  N6: Arduino_Uno.D3_PWM, S1.Pin_3, S1.Pin_4, R5-Taster.Pin_1
  N7: Arduino_Uno.5V, LED-Green.cathode, S1.Pin_1, S1.Pin_2, LED-Red.cathode, LED-White.cathode, LED-Yellow.cathode
  N8: LED-Green.anode, R3-Green.Pin_1
  N9: LED-Red.anode, R1-Red.Pin_1
  N10: LED-White.anode, R2-White.Pin_1
  N11: LED-Yellow.anode, R4-Yellow.Pin_1
